# Fritzing sketch singlebal_bb (saved by Fritzing 0.9.3b)
breadboards: 1

parts:
  Q1 = NPN-Transistor [package="TO92 [THT]"]
  Q2 = NPN-Transistor [package="TO92 [THT]"]
  Q3 = NPN-Transistor [package="TO92 [THT]"]  # not connected
  R1 = Resistor [tolerance=±5% resistance=220 package=THT]
  R2 = Resistor [tolerance=±5% resistance=220 package=THT]

nets:
  N1: Q1.E, R1.Pin_1
  N2: Q1.C, Q2.C
  N3: Q2.E, R2.Pin_1
  N4: R1.Pin_0, R2.Pin_0

notes:
  Vp
  1+
  W1
  W2
  2+
  GND
  1-
  2-
  M1
  M2
  M3
  R1
  R2
