# Fritzing sketch flash_adc-bb (saved by Fritzing 0.9.3b)
breadboards: 1

parts:
  U1 = OP482 - Low Power, High Speed JFET Quad Operational Amplifier [part_number=OP482]
  R1 = Resistor [tolerance=±5% resistance=10k package=THT]
  R3 = Resistor [tolerance=±5% resistance=10k package=THT]
  R4 = Resistor [tolerance=±5% resistance=10k package=THT]
  R5 = Resistor [tolerance=±5% resistance=10k package=THT]
  U2 = 74HC04_HEX_INVERTER [package=dil14]
  IC4 = IC, DIP package, 14 pins [chip_label="SN74HC08   "]
  IC5 = IC, DIP package, 14 pins [chip_label="  SN74HC32 "]

nets:
  N1: U1.-INA, R3.Pin_0, R5.Pin_1
  N2: U1.+INA, U1.+INB, U1.+INC
  N3: U1.-INB, R3.Pin_1, R4.Pin_0
  N4: U1.-INC, R1.Pin_0, R4.Pin_1
  N5: U2.1Y, IC4.pin1
  N6: U2.VCC, IC4.pin14, IC5.pin14
  N7: IC4.pin3, IC5.pin1
  N8: IC4.pin7, IC5.pin7
  N9: IC5.pin2, IC5.pin5

notes:
  10kΩ
  W1
  W2
  D2
  Vn
  D1
  D0
  GND
  D6
  D7
  Vp
