# Fritzing sketch heartbeat_bb (saved by Fritzing 0.9.3b)
breadboards: 1

parts:
  LED1 = LED - 5mm [color="Infrared (940nm)" package="5 mm [THT]"]
  LED2 = LED - 5mm [color="Blue (430nm)" package="5 mm [THT]"]
  R1 = Resistor [tolerance=±5% resistance=1k package=THT]
  R2 = Resistor [tolerance=±5% resistance=470 package=THT]
  R3 = Resistor [tolerance=±5% resistance=10k package=THT]
  R4 = Resistor [tolerance=±5% resistance=47k package=THT]
  C2 = Electrolytic Capacitor [capacitance=1µF package="100 mil [THT, electrolytic]"]
  R5 = Resistor [tolerance=±5% resistance=100 package=THT]
  C1 = Capacitor Polarized [package=cpol-radial-100uf-25v]
  C3 = Electrolytic Capacitor [capacitance=1µF package="100 mil [THT, electrolytic]"]
  R6 = Resistor [tolerance=±5% resistance=47k package=THT]
  IC2 = IC, DIP package, 14 pins [chip_label=OP484]

nets:
  N1: LED1.cathode, LED2.cathode, C2.-, IC2.pin3, IC2.pin10
  N2: LED1.anode, R1.Pin_1, C1.-
  N3: LED2.anode, R2.Pin_1
  N4: R1.Pin_0, R2.Pin_0, IC2.pin4
  N5: R3.Pin_0, R4.Pin_0, IC2.pin1
  N6: R3.Pin_1, C1.+, IC2.pin2
  N7: R4.Pin_1, C2.+, IC2.pin5
  N8: R5.Pin_0, IC2.pin6, IC2.pin7
  N9: R5.Pin_1, C3.-, R6.Pin_1, IC2.pin9
  N10: C3.+, R6.Pin_0, IC2.pin8

notes:
  Vp
  1+
  1-
  GND
  Vn
  470Ω
  1kΩ
  IR LED
  Photo-Tr
  47uF
  10kΩ
  47kΩ
  1uF
  100Ω
