# Fritzing sketch nmos_diode_bb (saved by Fritzing 0.9.3b)
breadboards: 1

parts:
  R1 = Resistor [tolerance=±5% resistance=100 package=THT]
  Q2 = NPN-Transistor [package="TO92 [THT]"]

nets:
  N1: R1.Pin_0, Q2.B, Q2.C

notes:
  1-
  1+
  2-
  W1
  2+
  Vn
  ZVN2110A
