# Fritzing sketch trans_stepup_bb (saved by Fritzing 0.9.3b)
breadboards: 1

parts:
  R1 = Resistor [tolerance=±5% resistance=400 package=THT]
  R2 = Resistor [tolerance=±5% resistance=100 package=THT]
  IC2 = IC, DIP package, 12 pins [chip_label=HPH1-1400]

nets:
  N1: R1.Pin_0, IC2.pin11
  N2: R1.Pin_1, IC2.pin6, IC2.pin7
  N3: R2.Pin_1, IC2.pin3
  N4: IC2.pin8, IC2.pin10

notes:
  GND
  1+
  1-
  2-
  2+
  W1
