# Fritzing sketch transtc_bb (saved by Fritzing 0.9.3b)
breadboards: 1

parts:
  R1 = Resistor [tolerance=±5% resistance=100 package=THT]
  R2 = Resistor [tolerance=±5% resistance=100 package=THT]
  IC1 = IC, DIP package, 12 pins [chip_label=HPH1-1400]

nets:
  N1: R1.Pin_0, IC1.pin12
  N2: R1.Pin_1, IC1.pin6, IC1.pin7
  N3: R2.Pin_1, IC1.pin1
  N4: IC1.pin2, IC1.pin4
  N5: IC1.pin3, IC1.pin5
  N6: IC1.pin8, IC1.pin10
  N7: IC1.pin9, IC1.pin11

notes:
  2+
  2-
  1-
  GND
  1+
  W1
